# Fritzing sketch kit stem carduino fritzing schematic and codes (saved by Fritzing 0.9.3b)
breadboards: 1

parts:
  U1 = atmega328 [package=dip]
  XTAL1 = Crystal [frequency="16 Mhz" package=THT]
  C1 = Ceramic Capacitor [capacitance=22pF package="0603 [SMD, multilayer]"]
  C2 = Ceramic Capacitor [capacitance=22pF package="0603 [SMD, multilayer]"]
  C3 = Ceramic Capacitor [capacitance="100 nF" package="0603 [SMD, multilayer]"]
  C6 = Ceramic Capacitor [capacitance="100 nF" package="0603 [SMD, multilayer]"]
  R1 = Resistor [tolerance=±5% resistance=10k package="2010 [SMD]"]
  S1 = Pushbutton [package="[SMD]"]
  C7 = Ceramic Capacitor [capacitance="100 nF" package="0603 [SMD, multilayer]"]
  R2 = Resistor [tolerance=±5% resistance=220 package="2010 [SMD]"]
  LED1 = smd LED [color="Red (633nm)" package="0603 [SMD]"]
  LED2 = LED - 5mm [color="Green (565nm)" package="5 mm [THT]"]
  R3 = Resistor [tolerance=±5% resistance=220 package="2010 [SMD]"]
  C8 = Capacitor Polarized [package=panasonic_c]
  Part1 = FTDI Basic Programmer
  IC1 = Voltage Regulator [package=to-220-alt]
  IC2 = L293D [package=THT]
  M1 = Getriebemotor
  M2 = Getriebemotor
  VCC1 = Battery block 9V
  C9 = Electrolytic Capacitor [capacitance=10µF voltage=35V package="0405 [SMD, electrolytic]"]
  C10 = Electrolytic Capacitor [capacitance=10μF voltage=50V package="0605 [SMD, electrolytic]"]  # not connected
  Part2 = Bluetooth HC-05 Macho

nets:
  N1: U1.RESET, R1.Pin_0, S1.Pin_1, S1.Pin_2, C7.1
  N2: U1.D0_(RX), Part1.TXO
  N3: U1.D1_(TX), Part1.RXI
  N4: U1.D2, Part2.TXD
  N5: U1.D3_(PWM), Part2.RXD
  N6: U1.VCC, R1.Pin_1
  N7: U1.XLAT1, XTAL1.pin_0, C2.0
  N8: U1.XLAT2, XTAL1.pin_1, C1.0
  N9: U1.D6_(PWM), IC2.Enable_1
  N10: U1.D7, IC2.In_1
  N11: U1.D8, IC2.In_2
  N12: U1.D9_(PWM), IC2.Enable_2
  N13: U1.D10_(PWM), IC2.In_3
  N14: U1.D11_(PWM), IC2.In_4
  N15: U1.D13, R2.Pin_1
  N16: U1.AVCC, C6.1, R3.Pin_1, C8.+, Part1.POWER, IC1.OUT, IC2.+V, C9.+, Part2.VCC
  N17: U1.AREF, C3.0
  GND: U1.GND#21, C1.1, C2.1, C3.1, C6.0, S1.Pin_3, S1.Pin_4, LED1.cathode, LED2.cathode, C8.-, Part1.GND, IC1.IN, IC2.0V, VCC1.-, C9.-, Part2.GND
  N18: C7.0, Part1.DTR
  N19: R2.Pin_0, LED1.anode
  N20: LED2.anode, R3.Pin_0
  N21: IC1.GND, IC2.+Vmotor, VCC1.+
  N22: IC2.Out_1_(_Controlled_by_Enable_1_), M2.pin_2
  N23: IC2.Out_2_(_Controlled_by_Enable_1_), M2.pin_1
  N24: IC2.Out_3_(_Controlled_by_Enable_2_), M1.pin_2
  N25: IC2.Out_4_(_Controlled_by_Enable_2_), M1.pin_1

notes:
  KIT STEM CarDuino
  by Chegu Sahrul Rashid

// code stored in the sketch: kit stem carduino.ino

#include<stdio.h>
#include<SoftwareSerial.h>
// BTSerial (Rx, Tx); Based on the Aduno board
SoftwareSerial bt(2, 3);

//left wheel
int pwm1 = 6;
int in1 = 7;
int in2 = 8;

//right wheel
int pwm2 = 9;
int in3 = 10;
int in4 = 11;

char data = 'S';
char prevdata = 'A';
int manmode(char data);
int vel = 255;


void setup() {
  //left wheel
  pinMode(pwm1, OUTPUT); //PWM-Pin
  pinMode(in1, OUTPUT); //IN1-Pin
  pinMode(in2, OUTPUT); //IN2-Pin
  //right wheel
  pinMode(pwm2, OUTPUT); //PWM-Pin
  pinMode(in3, OUTPUT); //IN1-Pin
  pinMode(in4, OUTPUT); //IN2-Pin
  //bluetooth
  bt.begin(9600);
  pinMode(LED_BUILTIN, OUTPUT);
}

void loop()
{
  char data;
  data = bt.read();
  manmode(data);
}

int manmode(char data)
{
  switch (data)
  {
    case 'F': front(); break;
    case 'B': rear(); break;
    case 'L': left(); break;
    case 'R': right(); break;
    case 'S' : brake(); break;
    case 'I' : rightfwd(); break;
    case 'J' : rightback(); break;
    case 'G' : leftfwd(); break;
    case 'H' : leftback(); break;
  }
}

void rightfwd()
{
  nav(vel, vel/2);

  return ;
}
void rightback()
{
  rev(vel, vel/2);
  return ;
}
void leftfwd()
{
  nav(vel/2, vel);
  return ;
}
void leftback()
{
  rev(vel/2, vel);
  return ;
}
void right()
{
  
  kanan();
  return ;
}
void left()
{
  kiri();
  return ;
}
void front()
{
  nav(vel, vel);
  return;
}
void rear()
{
  rev(vel, vel);
  return;
}
void brake()
{
  //nav(0, 0);
  brake(0, 0);
  return;
}

void nav(int spd, int spd2)
{
  analogWrite(pwm1, spd);
  digitalWrite(in1, HIGH);
  digitalWrite(in2, LOW);
  analogWrite(pwm2, spd2);
  digitalWrite(in3, HIGH);
  digitalWrite(in4, LOW);
}

void kanan()
{
  analogWrite(pwm1, vel);
  digitalWrite(in1, HIGH);
  digitalWrite(in2, LOW);
  analogWrite(pwm2, vel);
  digitalWrite(in3, LOW);
  digitalWrite(in4, HIGH);
}

void kiri()
{
  analogWrite(pwm1, vel);
  digitalWrite(in1, LOW);
  digitalWrite(in2, HIGH);
  analogWrite(pwm2, vel);
  digitalWrite(in3, HIGH);
  digitalWrite(in4, LOW);
}

void rev(int spd, int spd2)
{
  analogWrite(pwm1, spd);
  digitalWrite(in1, LOW);
  digitalWrite(in2, HIGH);
  analogWrite(pwm2, spd2);
  digitalWrite(in3, LOW);
  digitalWrite(in4, HIGH);
}


void brake(int spd, int spd2)
{
  analogWrite(pwm1, spd2);
  digitalWrite(in1, HIGH);
  digitalWrite(in2, HIGH);
  analogWrite(pwm2, spd);
  digitalWrite(in3, LOW);
  digitalWrite(in4, LOW);
}
